// Logisim project CSE 231 L PROJECT 1.circ as structural Verilog: 4 circuits, main circuit main
module main (
  input  A,
  input  B,
  input  C,
  input  D,
  output out_5
);

  wire and_ic_1_out_9, and_ic_1_out_10, and_ic_2_out_9, and_ic_2_out_10, and_ic_3_out_9, and_ic_3_out_10,
       and_ic_4_out_9, and_ic_4_out_10, and_ic_5_out_9, and_ic_5_out_10, and_ic_6_out_9, and_ic_6_out_10,
       and_ic_7_out_9, and_ic_7_out_10, and_ic_8_out_9, and_ic_8_out_10, not_1_out_7, not_1_out_8,
       not_1_out_9, not_1_out_10, not_2_out_7, not_2_out_8, not_2_out_9, not_2_out_10, or_1_out_9,
       or_1_out_10, or_3_out_9, or_3_out_10, or_4_out_9, or_4_out_10;

  NOT not_1 (
    .in_1(A), .in_2(B), .in_3(C), .in_4(A), .out_7(not_1_out_7), .out_8(not_1_out_8), .out_9(not_1_out_9),
    .out_10(not_1_out_10));  // open: in_5, in_6, out_11, out_12
  NOT not_2 (
    .in_1(A), .in_2(B), .in_3(C), .in_4(A), .out_7(not_2_out_7), .out_8(not_2_out_8), .out_9(not_2_out_9),
    .out_10(not_2_out_10));  // open: in_5, in_6, out_11, out_12
  AND_IC and_ic_1 (
    .in_1(not_1_out_7), .in_2(not_1_out_8), .in_3(C), .in_4(C), .in_5(not_1_out_7), .in_6(B),
    .in_7(not_1_out_9), .in_8(not_1_out_10), .out_9(and_ic_1_out_9), .out_10(and_ic_1_out_10));
  AND_IC and_ic_2 (
    .in_1(not_1_out_7), .in_2(B), .in_3(not_1_out_9), .in_4(A), .in_5(not_1_out_7), .in_6(B), .in_7(C),
    .in_8(not_1_out_10), .out_9(and_ic_2_out_9), .out_10(and_ic_2_out_10));
  AND_IC and_ic_3 (
    .in_1(not_1_out_7), .in_2(B), .in_3(C), .in_4(A), .in_5(A), .in_6(not_1_out_8), .in_7(not_1_out_9),
    .in_8(not_1_out_10), .out_9(and_ic_3_out_9), .out_10(and_ic_3_out_10));
  AND_IC and_ic_4 (
    .in_1(A), .in_2(not_2_out_8), .in_3(C), .in_4(not_2_out_10), .in_5(A), .in_6(not_2_out_8), .in_7(C),
    .in_8(A), .out_9(and_ic_4_out_9), .out_10(and_ic_4_out_10));
  AND_IC and_ic_5 (
    .in_1(A), .in_2(B), .in_3(not_2_out_9), .in_4(not_2_out_10), .in_5(A), .in_6(B), .in_7(not_2_out_9),
    .in_8(A), .out_9(and_ic_5_out_9), .out_10(and_ic_5_out_10));
  AND_IC and_ic_6 (
    .in_1(A), .in_2(B), .in_3(C), .in_4(not_2_out_10), .in_5(A), .in_6(B), .in_7(C), .in_8(A),
    .out_9(and_ic_6_out_9), .out_10(and_ic_6_out_10));
  AND_IC and_ic_7 (
    .in_1(not_1_out_7), .in_2(not_1_out_8), .in_3(not_1_out_9), .in_4(A), .in_5(not_1_out_7),
    .in_6(not_1_out_8), .in_7(C), .in_8(not_1_out_10), .out_9(and_ic_7_out_9), .out_10(and_ic_7_out_10));
  AND_IC and_ic_8 (
    .in_1(not_2_out_7), .in_2(B), .in_3(not_2_out_9), .in_4(A), .in_5(A), .in_6(not_2_out_8),
    .in_7(not_2_out_9), .in_8(A), .out_9(and_ic_8_out_9), .out_10(and_ic_8_out_10));
  OR or_1 (
    .in_1(and_ic_7_out_9), .in_2(and_ic_7_out_10), .in_3(and_ic_1_out_9), .in_4(and_ic_1_out_10),
    .in_5(and_ic_2_out_9), .in_6(and_ic_2_out_10), .in_7(and_ic_3_out_9), .in_8(and_ic_3_out_10),
    .out_9(or_1_out_9), .out_10(or_1_out_10));
  or or_2 (out_5, or_3_out_9, or_3_out_10);
  OR or_3 (
    .in_1(or_1_out_9), .in_2(or_1_out_10), .in_3(or_4_out_9), .in_4(or_4_out_10), .in_5(A), .in_6(C),
    .in_7(B), .in_8(A), .out_9(or_3_out_9), .out_10(or_3_out_10));
  OR or_4 (
    .in_1(and_ic_8_out_9), .in_2(and_ic_8_out_10), .in_3(and_ic_4_out_9), .in_4(and_ic_4_out_10),
    .in_5(and_ic_5_out_9), .in_6(and_ic_5_out_10), .in_7(and_ic_6_out_9), .in_8(and_ic_6_out_10),
    .out_9(or_4_out_9), .out_10(or_4_out_10));

  assign D = A;

  // Notes on the sheet:
  //   AB'C'D'
  //   A'BCD
  //   A'B'C'D
  //   A'B'CD'
  //   A'BC'D'
  //   A'B'CD
  //   A'BC'D
  //   A'BCD'
  //   AB'CD'
  //   AB'CD
  //   ABC'D
  //   ABC'D'
  //   ABCD'
  //   A'BC'D
  //   AB'C'D
endmodule

module AND_IC (
  input  in_1,
  input  in_2,
  input  in_3,
  input  in_4,
  input  in_5,
  input  in_6,
  input  in_7,
  input  in_8,
  output out_9,
  output out_10
);

  and and_1 (out_9, in_1, in_2, in_3, in_4);
  and and_2 (out_10, in_5, in_6, in_7, in_8);
endmodule

module OR (
  input  in_1,
  input  in_2,
  input  in_3,
  input  in_4,
  input  in_5,
  input  in_6,
  input  in_7,
  input  in_8,
  output out_9,
  output out_10
);

  or or_1 (out_10, in_5, in_6, in_7, in_8);
  or or_2 (out_9, in_1, in_2, in_3, in_4);
endmodule

module NOT (
  input  in_1,
  input  in_2,
  input  in_3,
  input  in_4,
  input  in_5,
  input  in_6,
  output out_7,
  output out_8,
  output out_9,
  output out_10,
  output out_11,
  output out_12
);

  not not_1 (out_7, in_1);
  not not_2 (out_8, in_2);
  not not_3 (out_9, in_3);
  not not_4 (out_10, in_4);
  not not_5 (out_11, in_5);
  not not_6 (out_12, in_6);
endmodule
