// Logisim project LAB-2.circ as structural Verilog
module C1 (
  input  A,
  input  A_2,
  input  B,
  input  A_3,
  input  B_2,
  output A_A__prime_A_prime,
  output AB,
  output out_8
);

  wire nand_2_out, nand_3_out, nand_4_out;

  nand nand_1 (A_A__prime_A_prime, A, A);
  nand nand_2 (nand_2_out, A_2, A_2, B);
  nand nand_3 (nand_3_out, A_3, A_3);
  nand nand_4 (nand_4_out, B_2, B_2);
  nand nand_5 (AB, nand_2_out, nand_2_out);
  nand nand_6 (out_8, nand_3_out, nand_4_out);

  // Notes on the sheet:
  //   1.
  //   (A.B)'
  //   A'
  //   B'
  //                (A'B')'= A+B
endmodule

module F1 (
  input  A,
  input  B,
  input  A_2,
  input  B_2,
  output out_5,
  output out_6
);

  wire nand_1_out, nand_2_out, nand_3_out, nand_4_out, nand_5_out, nand_6_out, nand_8_out;

  nand nand_1 (nand_1_out, A, B);
  nand nand_2 (nand_2_out, A_2, B_2);
  nand nand_3 (nand_3_out, A, nand_1_out);
  nand nand_4 (nand_4_out, nand_1_out, B, B);
  nand nand_5 (nand_5_out, A_2, nand_2_out);
  nand nand_6 (nand_6_out, nand_2_out, B_2);
  nand nand_7 (out_5, nand_3_out, nand_4_out);
  nand nand_8 (nand_8_out, nand_5_out, nand_6_out);
  nand nand_9 (out_6, nand_8_out, nand_8_out);

  // Notes on the sheet:
  //   XOR using NAND
  //   XNOR using NAND
  //   (AB)'
  //   (AB)'
  //                               ( B.(AB)')'= B'+ AB
  //   (A.(AB)')'= A'+AB
  //   (A.(AB)')'
  //                                          (A'+AB).(B'+AB)= A'B + AB'
  //   (B.(AB)')'
  //   ((A.(AB)')' . (B.(AB)')')'
  //   (A. (AB)')' .(B.(AB)')'
endmodule
