// Logisim project LAB1 CSE 231.circ as structural Verilog: 4 circuits, main circuit main
module main (
  input  A,
  input  B,
  input  C,
  output out_4
);

  wire ic_7404_1_out_7, ic_7404_1_out_8, ic_7408_1_out_9, ic_7408_1_out_10, ic_7408_1_out_12,
       ic_7432_1_out_12;

  IC_7404 ic_7404_1 (
    .in_1(A), .in_2(B), .out_7(ic_7404_1_out_7), .out_8(ic_7404_1_out_8));  // open: in_3, in_4, out_9, out_10, in_5, out_11, in_6, out_12
  IC_7408 ic_7408_1 (
    .in_1(ic_7404_1_out_7), .in_2(C), .in_3(A), .in_4(ic_7404_1_out_8), .in_7(B), .in_8(C),
    .out_9(ic_7408_1_out_9), .out_10(ic_7408_1_out_10), .out_12(ic_7408_1_out_12));  // open: in_5, in_6, out_11
  IC_7432 ic_7432_1 (
    .in_5(ic_7432_1_out_12), .in_6(ic_7408_1_out_12), .in_7(ic_7408_1_out_9), .in_8(ic_7408_1_out_10),
    .out_11(out_4), .out_12(ic_7432_1_out_12));  // open: in_1, in_2, in_3, in_4, out_9, out_10

  // Notes on the sheet:
  //   AB'
  //   A'C
endmodule

module IC_7408 (
  input  in_1,
  input  in_2,
  input  in_3,
  input  in_4,
  input  in_5,
  input  in_6,
  input  in_7,
  input  in_8,
  output out_9,
  output out_10,
  output out_11,
  output out_12
);

  and and_1 (out_9, in_1, in_2);
  and and_2 (out_10, in_3, in_4);
  and and_3 (out_11, in_5, in_6);
  and and_4 (out_12, in_7, in_8);
endmodule

module IC_7404 (
  input  in_1,
  input  in_2,
  input  in_3,
  input  in_4,
  input  in_5,
  input  in_6,
  output out_7,
  output out_8,
  output out_9,
  output out_10,
  output out_11,
  output out_12
);

  not not_1 (out_7, in_1);
  not not_2 (out_8, in_2);
  not not_3 (out_9, in_3);
  not not_4 (out_10, in_4);
  not not_5 (out_11, in_5);
  not not_6 (out_12, in_6);
endmodule

module IC_7432 (
  input  in_1,
  input  in_2,
  input  in_3,
  input  in_4,
  input  in_5,
  input  in_6,
  input  in_7,
  input  in_8,
  output out_9,
  output out_10,
  output out_11,
  output out_12
);

  or or_1 (out_9, in_1, in_2);
  or or_2 (out_10, in_3, in_4);
  or or_3 (out_11, in_5, in_6);
  or or_4 (out_12, in_7, in_8);
endmodule
