// Logisim project LAB 3B.circ as structural Verilog: 4 circuits, main circuit main
module main (
  input  B,
  input  C,
  input  in_3,
  output out_4
);

  wire ic_4075_or_1_out_11, ic_4075_or_1_out_12, ic_4075_or_2_out_10, ic_4075_or_2_out_11,
       ic_4075_or_2_out_12, ic_7404_not_1_out_7, ic_7404_not_1_out_10, ic_7404_not_1_out_11,
       ic_7411_and_1_out_12;

  IC_7404__not ic_7404_not_1 (
    .in_1(B), .in_4(C), .in_5(in_3), .out_7(ic_7404_not_1_out_7), .out_10(ic_7404_not_1_out_10),
    .out_11(ic_7404_not_1_out_11));  // open: in_2, in_3, in_6, out_8, out_9, out_12
  IC_4075__OR ic_4075_or_1 (
    .in_4(ic_7404_not_1_out_10), .in_5(ic_7404_not_1_out_11), .in_6(ic_7404_not_1_out_7),
    .in_7(ic_7404_not_1_out_10), .in_8(B), .in_9(ic_7404_not_1_out_11), .out_11(ic_4075_or_1_out_11),
    .out_12(ic_4075_or_1_out_12));  // open: in_1, in_2, in_3, out_10
  IC_4075__OR ic_4075_or_2 (
    .in_1(ic_7404_not_1_out_10), .in_2(in_3), .in_3(ic_7404_not_1_out_7), .in_4(C), .in_5(in_3),
    .in_6(ic_7404_not_1_out_7), .in_7(B), .in_8(in_3), .in_9(C), .out_10(ic_4075_or_2_out_10),
    .out_11(ic_4075_or_2_out_11), .out_12(ic_4075_or_2_out_12));
  IC_7411__AND ic_7411_and_1 (
    .in_4(ic_7411_and_1_out_12), .in_5(ic_4075_or_1_out_11), .in_6(ic_4075_or_2_out_10),
    .in_7(ic_4075_or_2_out_11), .in_8(ic_4075_or_1_out_12), .in_9(ic_4075_or_2_out_12), .out_11(out_4),
    .out_12(ic_7411_and_1_out_12));  // open: in_1, in_2, in_3, out_10

  // Notes on the sheet:
  //   A
endmodule

module IC_7404__not (
  input  in_1,
  input  in_2,
  input  in_3,
  input  in_4,
  input  in_5,
  input  in_6,
  output out_7,
  output out_8,
  output out_9,
  output out_10,
  output out_11,
  output out_12
);

  not not_1 (out_7, in_1);
  not not_2 (out_8, in_2);
  not not_3 (out_9, in_3);
  not not_4 (out_10, in_4);
  not not_5 (out_11, in_5);
  not not_6 (out_12, in_6);
endmodule

module IC_4075__OR (
  input  in_1,
  input  in_2,
  input  in_3,
  input  in_4,
  input  in_5,
  input  in_6,
  input  in_7,
  input  in_8,
  input  in_9,
  output out_10,
  output out_11,
  output out_12
);

  or or_1 (out_10, in_1, in_2, in_3);
  or or_2 (out_11, in_4, in_5, in_6);
  or or_3 (out_12, in_7, in_8, in_9);
endmodule

module IC_7411__AND (
  input  in_1,
  input  in_2,
  input  in_3,
  input  in_4,
  input  in_5,
  input  in_6,
  input  in_7,
  input  in_8,
  input  in_9,
  output out_10,
  output out_11,
  output out_12
);

  and and_1 (out_10, in_1, in_2, in_3);
  and and_2 (out_11, in_4, in_5, in_6);
  and and_3 (out_12, in_7, in_8, in_9);
endmodule
