// Logisim project lab 4.circ as structural Verilog: 4 circuits, main circuit main
module main (
  input  X,
  input  Y,
  input  Z,
  input  in_4,
  output A,
  output B,
  output C,
  output D
);

  wire ic_4075_1_out_9, ic_4075_1_out_12, ic_7404_1_out_11, ic_7404_1_out_12, ic_7411_1_out_9,
       ic_7411_1_out_10, ic_7411_1_out_11, ic_7411_1_out_12, ic_7411_2_out_9, ic_7411_2_out_10,
       ic_7411_2_out_11, ic_7411_2_out_12;

  IC_7404 ic_7404_1 (
    .in_4(in_4), .in_5(Z), .in_6(Y), .out_10(D), .out_11(ic_7404_1_out_11), .out_12(ic_7404_1_out_12));  // open: in_1, in_2, in_3, out_7, out_8, out_9
  IC_7411 ic_7411_1 (
    .in_1(ic_7404_1_out_12), .in_2(in_4), .in_3(ic_7404_1_out_12), .in_4(Z), .in_5(Z), .in_6(Y), .in_7(Y),
    .in_8(in_4), .out_9(ic_7411_1_out_9), .out_10(ic_7411_1_out_10), .out_11(ic_7411_1_out_11),
    .out_12(ic_7411_1_out_12));
  IC_7411 ic_7411_2 (
    .in_1(ic_7404_1_out_11), .in_2(D), .in_3(Z), .in_4(in_4), .in_5(D), .in_6(ic_7411_2_out_12), .in_7(Y),
    .in_8(ic_7404_1_out_11), .out_9(ic_7411_2_out_9), .out_10(ic_7411_2_out_10), .out_11(ic_7411_2_out_11),
    .out_12(ic_7411_2_out_12));
  IC_4075 ic_4075_1 (
    .in_1(ic_7411_1_out_9), .in_2(ic_7411_1_out_10), .in_3(ic_4075_1_out_9), .in_4(ic_7411_2_out_11),
    .in_5(ic_7411_1_out_11), .in_6(ic_4075_1_out_12), .in_7(ic_7411_1_out_12), .in_8(X),
    .out_9(ic_4075_1_out_9), .out_10(B), .out_11(A), .out_12(ic_4075_1_out_12));
  IC_4075 ic_4075_2 (
    .in_7(ic_7411_2_out_10), .in_8(ic_7411_2_out_9), .out_12(C));  // open: in_1, in_2, in_3, in_4, in_5, in_6, out_9, out_10, out_11

  // Notes on the sheet:
  //   W
  //   X'
  //   XZ
  //   Z'
  //   Y'
  //   XY
  //   x'y
  //   X'Z
endmodule

module IC_7404 (
  input  in_1,
  input  in_2,
  input  in_3,
  input  in_4,
  input  in_5,
  input  in_6,
  output out_7,
  output out_8,
  output out_9,
  output out_10,
  output out_11,
  output out_12
);

  not not_1 (out_7, in_1);
  not not_2 (out_8, in_2);
  not not_3 (out_9, in_3);
  not not_4 (out_10, in_4);
  not not_5 (out_11, in_5);
  not not_6 (out_12, in_6);
endmodule

module IC_7411 (
  input  in_1,
  input  in_2,
  input  in_3,
  input  in_4,
  input  in_5,
  input  in_6,
  input  in_7,
  input  in_8,
  output out_9,
  output out_10,
  output out_11,
  output out_12
);

  and and_1 (out_9, in_1, in_2);
  and and_2 (out_10, in_3, in_4);
  and and_3 (out_11, in_5, in_6);
  and and_4 (out_12, in_7, in_8);
endmodule

module IC_4075 (
  input  in_1,
  input  in_2,
  input  in_3,
  input  in_4,
  input  in_5,
  input  in_6,
  input  in_7,
  input  in_8,
  output out_9,
  output out_10,
  output out_11,
  output out_12
);

  or or_1 (out_9, in_1, in_2);
  or or_2 (out_10, in_3, in_4);
  or or_3 (out_11, in_5, in_6);
  or or_4 (out_12, in_7, in_8);
endmodule
