// Logisim project LAB 5 2.circ as structural Verilog: 2 circuits, main circuit main
module main (
  input  in_1,
  input  in_2,
  input  in_3,
  input  in_4,
  input  in_5,
  input  in_6,
  input  in_7,
  input  in_8,
  input  in_9,
  input  in_10,
  input  in_11,
  output out_12,
  output out_13,
  output out_14,
  output out_15,
  output out_16,
  output out_17
);

  wire and_1_out, and_2_out, ic_74283_1_out_10, ic_74283_1_out_11, ic_74283_1_out_12, ic_74283_1_out_13,
       ic_74283_1_out_14, or_1_out;

  IC_74283 ic_74283_1 (
    .in_1(in_9), .in_2(in_3), .in_3(in_4), .in_4(in_7), .in_5(in_5), .in_6(in_6), .in_7(in_1), .in_8(in_8),
    .in_9(in_2), .out_10(ic_74283_1_out_10), .out_11(ic_74283_1_out_11), .out_12(ic_74283_1_out_12),
    .out_13(ic_74283_1_out_13), .out_14(ic_74283_1_out_14));
  IC_74283 ic_74283_2 (
    .in_1(in_11), .in_2(in_10), .in_3(ic_74283_1_out_10), .in_4(in_10), .in_5(ic_74283_1_out_11),
    .in_6(in_10), .in_7(ic_74283_1_out_12), .in_8(in_10), .in_9(ic_74283_1_out_13), .out_10(out_16),
    .out_11(out_13), .out_12(out_17), .out_13(out_14), .out_14(out_15));
  and and_1 (and_1_out, ic_74283_1_out_11, ic_74283_1_out_13);
  and and_2 (and_2_out, ic_74283_1_out_12, ic_74283_1_out_13);
  or or_1 (or_1_out, and_1_out, and_2_out);
  or or_2 (in_10, ic_74283_1_out_14, or_1_out);

  assign out_12 = in_10;
endmodule

module IC_74283 (
  input  in_1,
  input  in_2,
  input  in_3,
  input  in_4,
  input  in_5,
  input  in_6,
  input  in_7,
  input  in_8,
  input  in_9,
  output out_10,
  output out_11,
  output out_12,
  output out_13,
  output out_14
);

  wire adder_1_cout, adder_2_cout, adder_3_cout, xor_1_out, xor_2_out, xor_3_out, xor_4_out;

  xor xor_1 (xor_1_out, in_3, in_1);
  xor xor_2 (xor_2_out, in_5, in_1);
  xor xor_3 (xor_3_out, in_7, in_1);
  xor xor_4 (xor_4_out, in_9, in_1);
  Adder #(.width(1)) adder_1 (.a(in_2), .b(xor_1_out), .out(out_10), .cin(in_1), .cout(adder_1_cout));
  Adder #(.width(1)) adder_2 (.a(in_4), .b(xor_2_out), .out(out_11), .cin(adder_1_cout), .cout(adder_2_cout));
  Adder #(.width(1)) adder_3 (.a(in_6), .b(xor_3_out), .out(out_12), .cin(adder_2_cout), .cout(adder_3_cout));
  Adder #(.width(1)) adder_4 (.a(in_8), .b(xor_4_out), .out(out_13), .cin(adder_3_cout), .cout(out_14));
endmodule
