// Logisim project full adder using a multi plexer.circ as structural Verilog: 2 circuits, main circuit main
module main (
  input  C,
  input  in_2,
  input  in_3,
  input  in_4,
  input  A,
  input  B,
  output SUM,
  output Carry
);

  wire not_1_out_7;

  NOT not_1 (
    .in_1(C), .out_7(not_1_out_7));  // open: in_2, in_3, in_4, in_5, in_6, out_8, out_9, out_10, out_11, out_12
  Multiplexer #(.select(2)) multiplexer_1 (
    .in0(C), .in1(not_1_out_7), .in2(not_1_out_7), .in3(C), .out(SUM), .sel({B, A}));  // open: en
  Multiplexer #(.select(2)) multiplexer_2 (
    .in0(in_2), .in1(C), .in2(C), .in3(in_3), .out(Carry), .sel({B, A}));  // open: en
endmodule

module NOT (
  input  in_1,
  input  in_2,
  input  in_3,
  input  in_4,
  input  in_5,
  input  in_6,
  output out_7,
  output out_8,
  output out_9,
  output out_10,
  output out_11,
  output out_12
);

  not not_1 (out_8, in_2);
  not not_2 (out_7, in_1);
  not not_3 (out_9, in_3);
  not not_4 (out_10, in_4);
  not not_5 (out_11, in_5);
  not not_6 (out_12, in_6);
endmodule
