// Logisim project F.1.1.circ as structural Verilog: 1 circuit, main circuit main
module main (
  input  x,
  output [1:0] out_2,
  output [1:0] out_3,
  output out_4
);

  wire and_1_out, clock_1_out, not_1_out, not_2_out;

  not not_1 (not_1_out, x);
  and and_1 (and_1_out, not_1_out, not_2_out);
  not not_2 (not_2_out, out_2[0]);
  Clock clock_1 (.out(clock_1_out));
  and and_2 (out_4, not_2_out, x);
  J_K_Flip_Flop j_k_ff_1 (.J(x), .clk(clock_1_out), .K(x), .Q(out_2[0]), .Qn(out_2[1]));  // open: preset, en, reset
  J_K_Flip_Flop j_k_ff_2 (
    .J(and_1_out), .clk(clock_1_out), .K(x), .Q(out_3[0]), .Qn(out_3[1]));  // open: preset, en, reset

  // Notes on the sheet:
  //   b
  //   a
endmodule
