// Logisim project lab 8 D flipflop.circ as structural Verilog: 1 circuit, main circuit main
module main (
  input  x,
  input  a,
  input  b
);

  wire clock_1_out, not_1_out, xor_1_out;

  ExactlyOne xor_1 (.out(xor_1_out), .in1(x), .in2(a), .in4(b));
  not not_1 (not_1_out, b);
  Clock clock_1 (.out(clock_1_out));
  D_Flip_Flop d_ff_1 (.clk(clock_1_out), .D(xor_1_out));  // open: Q, Qn, preset, en, reset
  D_Flip_Flop d_ff_2 (.clk(clock_1_out), .D(not_1_out));  // open: Q, Qn, preset, en, reset
endmodule
